// Logisim project numsec.circ as structural Verilog
module main (
  input  in_1,
  input  in_2,
  input  in_3,
  input  in_4,
  output out_5,
  output out_6,
  output out_7
);

  wire clock_1_out, numsec_1_borrow_s, numsec_1_carry_s, or_1_out, uc_1_count_enable, uc_1_count_mode,
       uc_1_ssd_min, uc_1_ssd_sec, verif_alarma_1_set_alarm;
  wire [3:0] transf_1_sec_unitati, transf_1_sec_zeci, transfmin_1_min_unitati, transfmin_1_min_zeci;
  wire [5:0] numsec_1_sec;
  wire [6:0] afisor_1_led_out, afisor_2_led_out, afisor_3_led_out, afisor_4_led_out, nummin_1_min;

  Clock clock_1 (.out(clock_1_out));
  uc uc_1 (
    .clk_1(clock_1_out), .rst(in_1), .start_stop(in_2), .m_button(in_3), .s_button(in_4),
    .alarma_activate(verif_alarma_1_set_alarm), .count_enable(uc_1_count_enable),
    .count_mode(uc_1_count_mode), .ssd_min(uc_1_ssd_min), .ssd_sec(uc_1_ssd_sec), .led_alarm(out_7));
  verif_alarma verif_alarma_1 (.sec(numsec_1_sec), .min(nummin_1_min), .set_alarm(verif_alarma_1_set_alarm));
  numsec numsec_1 (
    .clk_1(clock_1_out), .rst(in_1), .clk_enable(uc_1_count_enable), .count_mode(uc_1_count_mode),
    .sec(numsec_1_sec), .borrow_s(numsec_1_borrow_s), .carry_s(numsec_1_carry_s));
  or or_1 (or_1_out, numsec_1_borrow_s, numsec_1_carry_s);
  transf transf_1 (
    .enable(uc_1_ssd_sec), .sec(numsec_1_sec), .sec_ZECI(transf_1_sec_zeci),
    .sec_Unitati(transf_1_sec_unitati));
  transfmin transfmin_1 (
    .enable(uc_1_ssd_min), .min(nummin_1_min), .min_ZECI(transfmin_1_min_zeci),
    .min_Unitati(transfmin_1_min_unitati));
  nummin nummin_1 (
    .clk_1(clock_1_out), .rst(in_1), .clk_enable(or_1_out), .count_mode(uc_1_count_mode), .min(nummin_1_min),
    .borrow_m(out_5), .carry_m(out_6));
  afisor afisor_1 (.inputs(transf_1_sec_zeci), .LED_out(afisor_1_led_out));
  afisor afisor_2 (.inputs(transf_1_sec_unitati), .LED_out(afisor_2_led_out));
  afisor afisor_3 (.inputs(transfmin_1_min_zeci), .LED_out(afisor_3_led_out));
  afisor afisor_4 (.inputs(transfmin_1_min_unitati), .LED_out(afisor_4_led_out));
  _7_Segment_Display u_7_segment_display_1 (
    .g(afisor_1_led_out[0]), .f(afisor_1_led_out[1]), .a(afisor_1_led_out[6]), .b(afisor_1_led_out[5]),
    .e(afisor_1_led_out[2]), .d(afisor_1_led_out[3]), .c(afisor_1_led_out[4]));  // open: dp
  _7_Segment_Display u_7_segment_display_2 (
    .g(afisor_2_led_out[0]), .f(afisor_2_led_out[1]), .a(afisor_2_led_out[6]), .b(afisor_2_led_out[5]),
    .e(afisor_2_led_out[2]), .d(afisor_2_led_out[3]), .c(afisor_2_led_out[4]));  // open: dp
  _7_Segment_Display u_7_segment_display_3 (
    .g(afisor_3_led_out[0]), .f(afisor_3_led_out[1]), .a(afisor_3_led_out[6]), .b(afisor_3_led_out[5]),
    .e(afisor_3_led_out[2]), .d(afisor_3_led_out[3]), .c(afisor_3_led_out[4]));  // open: dp
  _7_Segment_Display u_7_segment_display_4 (
    .g(afisor_4_led_out[0]), .f(afisor_4_led_out[1]), .a(afisor_4_led_out[6]), .b(afisor_4_led_out[5]),
    .e(afisor_4_led_out[2]), .d(afisor_4_led_out[3]), .c(afisor_4_led_out[4]));  // open: dp
endmodule

// VHDL entity numsec, as the project stores it:
library ieee;
use ieee.std_logic_1164.all;
use ieee.numeric_std.all;
use ieee.std_logic_arith.all;
entity numsec is
    port ( 
        clk_1, rst : in std_logic;
        clk_enable : in std_logic;
        count_mode : in std_logic;
        sec: out  std_logic_vector (5 downto 0);
        borrow_s, carry_s : inout std_logic
    );
end numsec;

architecture Behavioral of numsec is

    signal count : integer range -2 to 60 := 0;
   
 
begin
    process (clk_1, rst,count_mode)
    variable count : integer range 0 to 60 := 0;
    begin
        if rst = '1' then
            count := 0;
            sec <= (others => '0');
            borrow_s <= '0';
            carry_s <= '0';
          end if;  
          if clk_enable = '1' then 
          if (count_mode = '1' and rising_edge(clk_1)) then -- Count up
                    count := count + 1;                    
                    if count = 59 then
                    
                    	carry_s <= '1';
               	else
               		carry_s <= '0';
               	end if;
               	
               	if count = 60 then
               		count := 0;
          		end if;
                    sec <= std_logic_vector(to_unsigned(count, 6));

                 
            elsif (count_mode='0' and rising_edge(clk_1)) then
            if(borrow_s='1') then
            count:=59;
            else count:=count-1;
            end if;
                     -- Count down
                  if count=0 then
            borrow_s<='1';
            else
            borrow_s<='0';
            end if;
            sec<= std_logic_vector(to_unsigned(count, 6));
                   end if;
                   end if;
    end process;
   
    
end architecture;

// VHDL entity transf, as the project stores it:
library IEEE;
use IEEE.STD_LOGIC_1164.ALL;
use IEEE.numeric_std.all;

entity transf is
    port (
    enable:in std_logic;
        sec: in std_logic_vector(5 downto 0);
        sec_ZECI: out std_logic_vector(3 downto 0);
        sec_Unitati: out std_logic_vector(3 downto 0)
    );
end transf;

architecture behavioral of transf is
    signal sec_nat: integer;
begin
    sec_nat <= to_integer(unsigned(sec));

    
    process(sec_nat)
    begin
    if enable='0' then
    		sec_ZECI<=x"0";
    		sec_Unitati<=x"0";
        elsif (sec_nat <= 9) then
            sec_ZECI <= "0000";
            sec_Unitati <= std_logic_vector(to_unsigned(sec_nat, 4));
        elsif (sec_nat >= 10 and sec_nat <= 19) then
            sec_ZECI <= "0001";
            sec_Unitati <= std_logic_vector(to_unsigned(sec_nat - 10, 4));
        elsif (sec_nat >= 20 and sec_nat <= 29) then
            sec_ZECI <= "0010";
            sec_Unitati <= std_logic_vector(to_unsigned(sec_nat - 20, 4));
        elsif (sec_nat >= 30 and sec_nat <= 39) then
            sec_ZECI <= "0011";
            sec_Unitati <= std_logic_vector(to_unsigned(sec_nat - 30, 4));
        elsif (sec_nat >= 40 and sec_nat <= 49) then
            sec_ZECI <= "0100";
            sec_Unitati <= std_logic_vector(to_unsigned(sec_nat - 40, 4));
        elsif (sec_nat >= 50 and sec_nat <= 59) then
            sec_ZECI <= "0101";
            sec_Unitati <= std_logic_vector(to_unsigned(sec_nat - 50, 4));
        end if;
    end process;
end behavioral;

// VHDL entity nummin, as the project stores it:
library ieee;
use ieee.std_logic_1164.all;
use ieee.numeric_std.all;

entity nummin is
    port ( 
        clk_1, rst : in std_logic;
        clk_enable : in std_logic;
        count_mode : in std_logic;
        min: out  std_logic_vector (6 downto 0);
        borrow_m, carry_m : inout std_logic
    );
end nummin;


architecture Behavioral of nummin is
begin
    process (clk_1, rst, count_mode)
        variable count : integer range -1 to 100 := 0;
    begin
        if rst = '1' then
            count := 0;
            min <= (others => '0');
            borrow_m <= '0';
            carry_m <= '0';
            end if;
        if clk_enable = '1' then
            if (count_mode = '1' and rising_edge(clk_1)) then
                   count := count + 1;                    
                    if count = 99 then
                    
                    	carry_m <= '1';
               	else
               		carry_m <= '0';
               	end if;
               	
               	if count = 100 then
               		count := 0;
          		end if;
                    min <= std_logic_vector(to_unsigned(count, 7));

            elsif (count_mode = '0' and rising_edge(clk_1)) then
                   if(borrow_m='1') then
            count:=99;
            else count:=count-1;
            end if;
                     -- Count down
                  if count=0 then
            borrow_m<='1';
            else
            borrow_m<='0';
            end if;
                    min <= std_logic_vector(to_unsigned(count, 7));
                end if;
            end if;
       
    end process;
end architecture;

// VHDL entity transfmin, as the project stores it:
library IEEE;
use IEEE.STD_LOGIC_1164.ALL;
use IEEE.numeric_std.all;

entity transfmin is
    port (
    enable:in std_logic;
        min: in std_logic_vector(6 downto 0);
        min_ZECI: out std_logic_vector(3 downto 0);
        min_Unitati: out std_logic_vector(3 downto 0)
    );
end transfmin;

architecture behavioral of transfmin is
    signal min_nat: integer;
begin
    min_nat <= to_integer(unsigned(min));
    
    process(min_nat)
    begin
    if enable='0' then
    min_ZECI<=x"0";
    min_Unitati<=x"0";
        elsif (min_nat <= 9) then
            min_ZECI <= "0000";
            min_Unitati <= std_logic_vector(to_unsigned(min_nat, 4));
        elsif (min_nat >= 10 and min_nat <= 19) then
            min_ZECI <= "0001";
            min_Unitati <= std_logic_vector(to_unsigned(min_nat - 10, 4));
        elsif (min_nat >= 20 and min_nat <= 29) then
            min_ZECI <= "0010";
            min_Unitati <= std_logic_vector(to_unsigned(min_nat - 20, 4));
        elsif (min_nat >= 30 and min_nat <= 39) then
            min_ZECI <= "0011";
            min_Unitati <= std_logic_vector(to_unsigned(min_nat - 30, 4));
        elsif (min_nat >= 40 and min_nat <= 49) then
            min_ZECI <= "0100";
            min_Unitati <= std_logic_vector(to_unsigned(min_nat - 40, 4));
        elsif (min_nat >= 50 and min_nat <= 59) then
            min_ZECI <= "0101";
            min_Unitati <= std_logic_vector(to_unsigned(min_nat - 50, 4));
        elsif (min_nat >= 60 and min_nat <= 69) then
            min_ZECI <= "0110";
            min_Unitati <= std_logic_vector(to_unsigned(min_nat - 60, 4));
        elsif (min_nat >= 70 and min_nat <= 79) then
            min_ZECI <= "0111";
            min_Unitati <= std_logic_vector(to_unsigned(min_nat - 70, 4));
        elsif (min_nat >= 80 and min_nat <= 89) then
            min_ZECI <= "1000";
            min_Unitati <= std_logic_vector(to_unsigned(min_nat - 80, 4));
        elsif (min_nat >= 90 and min_nat <= 99) then
            min_ZECI <= "1001";
            min_Unitati <= std_logic_vector(to_unsigned(min_nat - 90, 4));
        end if;
    end process;
end architecture;

// VHDL entity afisor, as the project stores it:
library IEEE;
use IEEE.STD_LOGIC_1164.ALL;
use IEEE.std_logic_unsigned.all;

entity afisor is
    Port ( inputs: in std_logic_vector(3 downto 0);
		LED_out : out std_logic_vector(6 downto 0));    -- Cathode patterns of 7-segment display
end afisor;

architecture Behavioral of afisor is

signal LED_BCD: STD_LOGIC_VECTOR (3 downto 0);


begin
LED_bcd<=inputs;
-- VHDL code for BCD to 7-segment decoder
-- Cathode patterns of the 7-segment LED display 
process(LED_BCD)
begin
    case LED_BCD is
    when "0000" => LED_out <= "1111110"; -- "0"     
    when "0001" => LED_out <= "0110000"; -- "1" 
    when "0010" => LED_out <= "1101101"; -- "2" 
    when "0011" => LED_out <= "1111001"; -- "3" 
    when "0100" => LED_out <= "0110011"; -- "4" 
    when "0101" => LED_out <= "1011011"; -- "5" 
    when "0110" => LED_out <= "1011111"; -- "6" 
    when "0111" => LED_out <= "1110000"; -- "7" 
    when "1000" => LED_out <= "1111111"; -- "8"     
    when "1001" => LED_out <= "1111011"; -- "9" 
	when others => LED_out <= "0000000";
    end case;
end process;

end Behavioral;

// VHDL entity uc, as the project stores it:
LIBRARY ieee;
USE ieee.std_logic_1164.all;

ENTITY uc IS

  port (
        clk_1: in std_logic;
        rst: in std_logic;
        start_stop: in std_logic;
        m_button: in std_logic;
        s_button: in std_logic;
        --carry,borrow: in std_logic;
        count_enable,count_mode,ssd_min,ssd_sec: inout std_logic;
        alarma_activate: in std_logic;
        led_alarm:out std_logic
    );
END uc;


ARCHITECTURE TypeArchitecture OF uc IS
type state_type is (Zero, Crescator,afisare_sec,afisare_min,afisare_min_sec,Descrescator,Alarma);
signal current_state, next_state:state_type:=Zero;

signal alarm_T5: std_logic:='0';

BEGIN

 process(rst,clk_1)
begin
 if (rst='1') then 
       current_state<=Zero;
 elsif (rising_edge(clk_1)) then 
 current_state<=next_state;
 end if;
 end process;



 
 process(start_stop,m_button,s_button,alarma_activate,alarm_T5)
 begin
 case current_state is
 when Zero => if start_stop='1' then
               next_state<=Crescator;
               else 
               next_state<=Zero;
               end if;
 when Crescator =>if m_button='1' and s_button='1' then 
 				next_state<=afisare_min_sec;
 				elsif m_button='1' then
                   next_state<=afisare_min;
                   elsif s_button='1' then
                   next_state<=afisare_sec;
                   else
                   next_state<=Crescator;
                   end if;
when afisare_min=> if s_button='1' then
 				next_state<=afisare_min_sec;
 				else
 				next_state<=afisare_min;
 				end if;
 				if alarma_activate='1' then
                   next_state<=Alarma;
                   end if;
when afisare_sec=> if m_button='1' then
				next_state<=afisare_min_sec;
				else 
				next_state<=afisare_sec;
				end if;
				if alarma_activate='1' then
                   next_state<=Alarma;
                   end if;
when afisare_min_sec=> if start_stop='1' then
					next_state<=Descrescator;
					else
					next_state<=afisare_min_sec;
					end if;
					if alarma_activate='1' then
                   next_state<=Alarma;
                   end if;
when Descrescator=>if m_button='1' and s_button='1' then 
 				next_state<=afisare_min_sec;
				elsif m_button='1' then
                   next_state<=afisare_min;
                   elsif s_button='1' then
                   next_state<=afisare_sec;
                   else
                   next_state<=Descrescator;
                   end if;
                   if alarma_activate='1' then
                   next_state<=Alarma;
                   end if;
 when Alarma=> if alarm_T5='1' then
 next_state<=Zero;
 else next_state<=Alarma;
 end if;
when others=> next_state<=Zero;
end case;
 end process;

process(current_state,clk_1)
variable count:integer:=0;
begin
if current_state=Alarma then
if clk_1='1' and clk_1'event then
if count=5 then
alarm_T5<='1';
count:=0;
else count:=count+1;
end if;
elsif current_state=Zero then
alarm_T5<='0';
end if;
end if;
end process;
 
process(current_state)
begin
case current_state is
when Zero=> count_enable<='0';
		count_mode<='0';
		ssd_min<='0';
		ssd_sec<='0';
		led_alarm<='0';
when Crescator=> count_mode<='1';
                 count_enable<='1';
when afisare_min=> ssd_min<='1';
				ssd_sec<='0';
when afisare_sec=>ssd_sec<='1';
				ssd_min<='0';
when afisare_min_sec=>ssd_sec<='1';
				ssd_min<='1';
when Descrescator=> count_mode<='0';
 				count_enable<='1';
 				ssd_min<='0';
 				ssd_sec<='0';
when Alarma=>led_alarm<='1';
			count_enable<='0';
			ssd_sec<='0';--0
			ssd_min<='0';
when others=>
end case;
end process;
           

END TypeArchitecture;

// VHDL entity verif_alarma, as the project stores it:
LIBRARY ieee;
USE ieee.std_logic_1164.all;

ENTITY verif_alarma IS
  PORT (
  ------------------------------------------------------------------------------
  --Insert input ports below
                      -- input bit example
   sec:in std_logic_vector(5 downto 0);
   min:in std_logic_vector(6 downto 0);
   set_alarm: out std_logic
    );
END verif_alarma;

--------------------------------------------------------------------------------
--Complete your VHDL description below
--------------------------------------------------------------------------------

ARCHITECTURE TypeArchitecture OF verif_alarma IS

signal min_sec: std_logic_vector(12 downto 0);

BEGIN
min_sec<=min & sec;
set_alarm<=not(min_sec(12) or min_sec(11) or min_sec(10) or min_sec(9) or min_sec(8) or min_sec(7) or min_sec(6) or min_sec(5) or min_sec(4) or min_sec(3) or min_sec(2) or min_sec(1) or min_sec(0));
END TypeArchitecture;
